# Fritzing sketch wwvb (saved by Fritzing 0.9.2b)

parts:
  Part1 = Arduino Nano (Rev3.0)
  U1 = attiny85 [package=dip]
  U2 = LM 358 Dual Op-Amp [package="DIP8 [THT]"]
  ANT1 = Antenna
  Part3 = Arduino Nano (Rev3.0)
  ANT3 = Antenna
  LED1 = Ruby the Red LED
  R = Resistor [tolerance=±5% resistance=110 package="2010 [SMD]"]
  C = Ceramic Capacitor [capacitance=1µF package="100 mil [THT, multilayer]"]
  R1 = Resistor [tolerance=±5% resistance=13k package=THT]
  R3 = Resistor [tolerance=±5% resistance=2.7k package=THT]
  Rf = Resistor [tolerance=±5% resistance=16k package=THT]
  R2 = Resistor [tolerance=±5% resistance=300 package=THT]
  R4 = Resistor [tolerance=±5% resistance=110 package=THT]
  Part4 = Arduino Nano (Rev3.0)
  U3 = attiny85 [package=dip]
  U4 = LM 358 Dual Op-Amp [package="DIP8 [THT]"]
  ANT4 = Antenna
  Rf_2 = Resistor [tolerance=±5% resistance=9.1k package=THT]
  R2_2 = Resistor [tolerance=±5% resistance=1k package=THT]
  R1_2 = Resistor [tolerance=±5% resistance=8.2k package=THT]

nets:
  N1: Part1.GND, U1.Pin_4, U2.connector2, U2.connector3
  N2: Part1.D9, R2.Pin_1
  N3: Part1.5V, U1.Pin_8, U2.connector7, R3.Pin_1
  N4: U1.Pin_3, R1.Pin_1
  N5: U2.connector0, ANT1.antenna_lead, Rf.Pin_0
  N6: U2.connector1, R1.Pin_0, R3.Pin_0, Rf.Pin_1, R2.Pin_0
  N7: Part3.GND, LED1.anode, C.1
  N8: Part3.D9, ANT3.antenna_lead, R.Pin_0, R4.Pin_0
  N9: LED1.cathode, R.Pin_1, C.0, R4.Pin_1
  N10: Part4.GND, U3.Pin_4, U4.connector2, U4.connector3
  N11: Part4.D9, R2_2.Pin_1
  N12: Part4.5V, U3.Pin_8, U4.connector7
  N13: U3.Pin_3, R1_2.Pin_1
  N14: U4.connector0, ANT4.antenna_lead, Rf_2.Pin_0
  N15: U4.connector1, Rf_2.Pin_1, R2_2.Pin_0, R1_2.Pin_0

notes:
  Amplitude Modulation using a summing op amp w/ DC offset
  Amplitude Modulation using internal PWM
  magenta : modulation signal
  cyan : carrier signal
  blue : modulated output
  Note : DEBUG circuit (LPF circuit) not required
  Amplitude Modulation using a summing op amp
